# Fritzing sketch cs_01 (saved by Fritzing 0.9.9b)
breadboards: 1

parts:
  Mod1 = Raspberry Pi Pico
  U1 = 74x125 [part_number=74x125 package="DIP (Dual Inline) [THT]"]
  Part1 = 74x125 [part_number=74x125 package="DIP (Dual Inline) [THT]"]  # not connected
  U1_1 = 74x125 [part_number=74x125 package="DIP (Dual Inline) [THT]"]  # not connected
  U1_2 = 74x125 [part_number=74x125 package="DIP (Dual Inline) [THT]"]  # not connected
  U1_3 = 74x125 [part_number=74x125 package="DIP (Dual Inline) [THT]"]  # not connected
  U1_4 = 74x125 [part_number=74x125 package="DIP (Dual Inline) [THT]"]  # not connected
  J1 = Screw terminal - 2 pins [package=THT]
  J3 = Camdenboss CTB0158-3 [part_number=CTB0158-3 package=THT]

nets:
  N1: Mod1.pin_3, Mod1.pin_8, Mod1.pin_13, Mod1.pin_18, Mod1.pin_23, Mod1.pin_28, Mod1.pin_33, Mod1.pin_38, Mod1.pin_42, U1.connector0, J1.pin1, J3.terminal_2
  N2: Mod1.pin_4, U1.connector1
  N3: Mod1.pin_40, U1.connector13
  N4: U1.connector2, J1.pin2, J3.terminal_1

notes:
  DCC Booster CDE Interface
  C - Data
  D - Ground
  E - Short Indication
  C
  D
  E

custom parts:
  Raspberry Pi Pico: Raspberry Pi Pico. Based around the RP2040 microcontroller the Pico is a low cost microcontroller device bringing Raspberry Pi quality, cost, and easy of use to the microcontroller space. Jan 2021, Split part in to two versions: tht (this one) and SMD. This one will drill holes for a .1 in header in pcb to allow plugging in the module as well as providing pads to solder the module to the top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
  74x125: 74x125 quad tristate buffer active low enable. The 74ahc125 variety is useful as a level translator as the inputs are 5V tolorant when run with a VCC of 3.3V (and will thus take a 5V signal in and provide a 3.3V signal out.) As well this part uses schematic subparts so you can drag each of the 4 gates to a different place in schematic view. Note having many (around 10 or more) subpart parts in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
  74x125: 74x125 quad tristate buffer active low enable. The 74ahc125 variety is useful as a level translator as the inputs are 5V tolorant when run with a VCC of 3.3V (and will thus take a 5V signal in and provide a 3.3V signal out.) As well this part uses schematic subparts so you can drag each of the 4 gates to a different place in schematic view. Note having many (around 10 or more) subpart parts in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
  74x125: 74x125 quad tristate buffer active low enable. The 74ahc125 variety is useful as a level translator as the inputs are 5V tolorant when run with a VCC of 3.3V (and will thus take a 5V signal in and provide a 3.3V signal out.) As well this part uses schematic subparts so you can drag each of the 4 gates to a different place in schematic view. Note having many (around 10 or more) subpart parts in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
  74x125: 74x125 quad tristate buffer active low enable. The 74ahc125 variety is useful as a level translator as the inputs are 5V tolorant when run with a VCC of 3.3V (and will thus take a 5V signal in and provide a 3.3V signal out.) As well this part uses schematic subparts so you can drag each of the 4 gates to a different place in schematic view. Note having many (around 10 or more) subpart parts in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
  74x125: 74x125 quad tristate buffer active low enable. The 74ahc125 variety is useful as a level translator as the inputs are 5V tolorant when run with a VCC of 3.3V (and will thus take a 5V signal in and provide a 3.3V signal out.) As well this part uses schematic subparts so you can drag each of the 4 gates to a different place in schematic view. Note having many (around 10 or more) subpart parts in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
  74x125: 74x125 quad tristate buffer active low enable. The 74ahc125 variety is useful as a level translator as the inputs are 5V tolorant when run with a VCC of 3.3V (and will thus take a 5V signal in and provide a 3.3V signal out.) As well this part uses schematic subparts so you can drag each of the 4 gates to a different place in schematic view. Note having many (around 10 or more) subpart parts in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
